# Fritzing sketch rc_lights_controller (saved by Fritzing 0.9.2b)
circuit board: 2.99803cm x 3.61244cm
breadboards: 1

parts:
  Q4 = NPN-Transistor [part_number=BC337-40 package="TO92 [THT]"]
  Q5 = NPN-Transistor [part_number=BC337-40 package="TO92 [THT]"]
  R2 = Resistor [tolerance=±5% resistance=3.3k package=THT]
  R3 = Resistor [tolerance=±5% resistance=470 package=THT]
  J1 = double row male pin header, 2 pins [form="♂ (male)"]
  S1 = Pushbutton [package="[THT]"]
  J2 = shrouded pin header, 6 pins [form="♂ (shrouded male)"]
  U1 = attiny85 [package=dip]
  J3 = double row male pin header, 2 pins [form="♂ (male)"]
  J4 = double row male pin header, 2 pins [form="♂ (male)"]
  Q6 = npn-Powertransistor [part_number=BD139-16 package="TO220 [THT]"]

nets:
  N1: Q4.E, Q6.base
  N2: Q4.B, R2.Pin_0
  N3: Q4.C, J1.pin1, Q6.collector
  N4: Q5.E, S1.Pin_3, S1.Pin_4, J2.pin3, J2.pin4, U1.Pin_4, J4.pin2, Q6.emitter
  N5: Q5.B, R3.Pin_0
  N6: Q5.C, J1.pin2
  N7: R2.Pin_1, U1.Pin_2
  N8: R3.Pin_1, U1.Pin_3
  N9: S1.Pin_1, U1.Pin_5
  N10: J2.pin1, U1.Pin_6
  N11: J2.pin2, J2.pin5, U1.Pin_8
  N12: J2.pin6, U1.Pin_7
  N13: J3.pin1, J3.pin2, J4.pin1

notes:
  12V
  +
  -
  OUTPUT_1 GND
  OUTPUT_2 GND
  INPUT_1
  INPUT_2
  GND
  +5V
  +12V
  OUTPUT_1 +
  OUTPUT_2 +
